# Fritzing sketch ScriptieDrawing (saved by Fritzing 0.9.3b)
circuit board: 5.50885cm x 5.72476cm
breadboards: 1

parts:
  Microcontroller = Arduino Uno (Rev3)
  Ultrasonic_Sensor = HC-SR04 Ultrasonic Distance Sensor
  D3 = Rectifier Diode [part_number=1N4001 package="300 mil [THT]"]
  D4 = Rectifier Diode [part_number=1N4001 package="300 mil [THT]"]
  MR = DC Motor
  ML = DC Motor
  VCC1 = Battery block 9V
  VCC2 = Battery block 9V
  R1 = Resistor [tolerance=±5% resistance=100 package=THT]
  LDR1 = Photocell (LDR) [package=THT]
  LED = LED - 5mm [color="White (4500K)" package="5 mm [THT]"]
  R2 = Resistor [tolerance=±5% resistance=0 package=THT]
  Q3 = PNP-Transistor [package="TO92 [THT]"]
  Q4 = PNP-Transistor [package="TO92 [THT]"]

nets:
  N1: Microcontroller.A0, R1.Pin_1, LDR1.pin_0
  N2: Microcontroller.D8, Ultrasonic_Sensor.GND
  N3: Microcontroller.GND, Ultrasonic_Sensor.ECHO, VCC1.-, VCC2.-, R1.Pin_0, LDR1.pin_1, R2.Pin_1, Q3.C, Q4.C
  N4: Microcontroller.D2, LED.anode
  N5: Microcontroller.D5_PWM, Q3.B
  N6: Microcontroller.D6_PWM, Q4.B
  N7: Microcontroller.D7, Ultrasonic_Sensor.TRIG
  5V: Microcontroller.5V, Ultrasonic_Sensor.VCC, VCC2.+
  N8: D3.cathode, D4.cathode, MR.pin_2, ML.pin_1, VCC1.+
  N9: D3.anode, ML.pin_2, Q3.E
  N10: D4.anode, MR.pin_1, Q4.E
  N11: LED.cathode, R2.Pin_0
